# Fritzing sketch thermometer-sketch-breadboard (saved by Fritzing 0.7.12b)
breadboards: 1

parts:
  Arduino1 = Arduino
  LCD1 = LCD screen
  R1 = Resistor [tolerance=±5% resistance=330 package=THT]
  C1 = Ceramic Capacitor [capacitance=4.7µF voltage=20V package="100 mil [THT, multilayer]"]
  R2 = Resistor [tolerance=±1% resistance=10k package=THT]

nets:
  N1: Arduino1.D12, LCD1.R/W
  N2: Arduino1.D11, LCD1.DB0
  N3: Arduino1.D9, LCD1.RS
  N4: Arduino1.D5, LCD1.DB5
  N5: Arduino1.D4, LCD1.DB6
  N6: Arduino1.D3, LCD1.DB7
  +5V: Arduino1.+5V, LCD1.VDD, R1.Pin_1, C1.1
  GND: Arduino1.GND, LCD1.VSS, LCD1.E, LCD1.LED-, R2.Pin_1
  N7: Arduino1.A0, C1.0, R2.Pin_0
  N8: LCD1.LED+, R1.Pin_0

notes:
  1
  Analog Input
