# Fritzing sketch thermometer-sketch (saved by Fritzing 0.7.12b)
breadboards: 1

parts:
  Thermistor = 220 Ω Resistor [package=THT]
  R1 = Resistor [tolerance=±5% resistance=220 package=THT]
  9V_Battery = Battery
  Arduino1 = Arduino
  LCD1 = LCD screen
  330Ω = Resistor [tolerance=±5% resistance=330 package=THT]

nets:
  N1: Thermistor.Pin_0, 330Ω.Pin_1
  GND: R1.Pin_1, 9V_Battery.-, Arduino1.GND, LCD1.VSS, LCD1.R/W, LCD1.LED-
  N2: 9V_Battery.+, Arduino1.VIN
  N3: Arduino1.D12, LCD1.RS
  N4: Arduino1.D11, LCD1.E
  N5: Arduino1.D9, LCD1.V0
  N6: Arduino1.D6, LCD1.DB4
  N7: Arduino1.D5, LCD1.DB5
  N8: Arduino1.D4, LCD1.DB6
  N9: Arduino1.D3, LCD1.DB7
  +5V: Arduino1.+5V, LCD1.VDD
  N10: LCD1.LED+, 330Ω.Pin_0

notes:
  Analog Input

custom parts:
  220 Ω Resistor: A generic resistor (0.25W)
